# Fritzing sketch Shema spajanja (saved by Fritzing 0.9.3b)
circuit board: 3.03859cm x 2.45533cm
breadboards: 1

parts:
  Rotacijski_enkoder = Rotary Encoder [package=THT]
  T1 = Pushbutton [package="[THT]"]
  T2 = Pushbutton [package="[THT]"]
  T3 = Pushbutton [package="[THT]"]
  T4 = Pushbutton [package="[THT]"]
  R7 = Resistor [tolerance=±5% resistance=1k package="0805 [SMD]"]
  R8 = Resistor [tolerance=±5% resistance=1k package="0805 [SMD]"]
  R9 = Resistor [tolerance=±5% resistance=1k package="0805 [SMD]"]
  R11 = Resistor [tolerance=±5% resistance=1k package=THT]
  Q3 = NPN-Transistor [package="TO92 [THT]"]
  R12 = Resistor [tolerance=±5% power=0.25 resistance=220 package=THT]
  R13 = Resistor [tolerance=±5% power=0.25 resistance=220 package=THT]
  R14 = Resistor [tolerance=±5% power=0.25 resistance=10k package=THT]
  R15 = Resistor [tolerance=±5% power=0.25 resistance=10k package=THT]
  R16 = Resistor [tolerance=±5% power=0.25 resistance=10k package=THT]
  R17 = Resistor [tolerance=±5% power=0.25 resistance=10k package=THT]
  Q4 = NPN-Transistor [package="TO92 [THT]"]
  Potenciometar = Rotary Potentiometer (Small) [maximum_resistance=10kΩ package=THT]
  <--_3_5mm_IN = Audio Jack (TRS) 3.5mm [package="4Ucon 08780 [THT]"]
  PICO1 = Raspberry Pi Pico
  PICO2 = Raspberry Pi Pico
  ILI9341_displej_sa_čitačem_za_SD_karticu = Color 320x240 TFT Display, ILI9341 Controller Chip
  Eksterni_izvor = 4 x AAA Battery Mount

nets:
  N1: Rotacijski_enkoder.EncoderPinA, PICO1.pin_12
  N2: Rotacijski_enkoder.EncoderPinC, PICO1.pin_7
  N3: Rotacijski_enkoder.EncoderPinB, PICO1.pin_6
  N4: T1.Pin_1, T1.Pin_2, T2.Pin_1, T2.Pin_2, T3.Pin_1, T3.Pin_2, T4.Pin_1, T4.Pin_2, Potenciometar.leg2, <--_3_5mm_IN.Sleeve, PICO1.pin_33, PICO1.pin_38, PICO1.pin_42, PICO2.pin_23, ILI9341_displej_sa_čitačem_za_SD_karticu.GND, Eksterni_izvor.-
  N5: T1.Pin_3, T1.Pin_4, R7.Pin_1
  N6: T2.Pin_3, T2.Pin_4, R8.Pin_1
  N7: T3.Pin_3, T3.Pin_4, R9.Pin_1
  N8: T4.Pin_3, T4.Pin_4, R11.Pin_1
  N9: R7.Pin_0, R8.Pin_0, R9.Pin_0, R11.Pin_0, PICO1.pin_36, ILI9341_displej_sa_čitačem_za_SD_karticu.VCC
  N10: Q3.E, <--_3_5mm_IN.Ring
  N11: Q3.B, R16.Pin_0, R17.Pin_0
  N12: Q3.C, R12.Pin_0
  N13: R12.Pin_1, R13.Pin_1, Potenciometar.wiper
  N14: R13.Pin_0, Q4.C
  N15: R14.Pin_0, R15.Pin_0, Q4.B
  N16: R14.Pin_1, R15.Pin_1, PICO2.pin_4
  N17: R16.Pin_1, R17.Pin_1, PICO2.pin_5
  N18: Q4.E, <--_3_5mm_IN.Tip
  N19: Potenciometar.leg1, Eksterni_izvor.+
  N20: PICO1.pin_16, PICO2.pin_22
  N21: PICO1.pin_17, PICO2.pin_21
  N22: PICO1.pin_20, ILI9341_displej_sa_čitačem_za_SD_karticu.D/C
  N23: PICO1.pin_21, ILI9341_displej_sa_čitačem_za_SD_karticu.MISO
  N24: PICO1.pin_22, ILI9341_displej_sa_čitačem_za_SD_karticu.CS
  N25: PICO1.pin_24, ILI9341_displej_sa_čitačem_za_SD_karticu.SCK
  N26: PICO1.pin_25, ILI9341_displej_sa_čitačem_za_SD_karticu.MOSI
  N27: PICO1.pin_26, ILI9341_displej_sa_čitačem_za_SD_karticu.Reset

custom parts:
  Raspberry Pi Pico: Raspberry Pi Pico. Based around the RP2040 microcontroller the Pico is a low cost microcontroller device bringing Raspberry Pi quality, cost, and easy of use to the microcontroller space. Jan 2021, Split part in to two versions: tht (this one) and SMD. This one will drill holes for a .1 in header in pcb to allow plugging in the module as well as providing pads to solder the module to the top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
  Color 320x240 TFT Display, ILI9341 Controller Chip: 2.2" TFT Display with ILI9341 Controller
